# Fritzing sketch final_circuit_v1 (saved by Fritzing 0.8.7b)

parts:
  Station_2Β = Microbit
  LCD1 = LCD screen
  U1 = 4-Channel 5v Relay Shield [package=relay-4ch5v10a]
  LCM1602_IIC1 = LCM1602 IIC [part_number="LCM1602 IIC" chip_label="LCM1602 IIC" package="DIP (Dual Inline) [THT]"]
  VCC1 = 4 x AAA Battery Mount
  J1 = Piezo Speaker  # not connected
  buzzer_module = mystery part, 3 pins [chip_label=?]
  VCC2 = Battery
  Earthquake_Sensor = Microbit
  VCC3 = Battery
  Station_2Α = Microbit
  VCC4 = Battery

nets:
  N1: Station_2Β.P0, buzzer_module.pin2
  N2: Station_2Β.P13, U1.IN4
  N3: Station_2Β.P14, U1.IN3
  N4: Station_2Β.P15, U1.IN2
  N5: Station_2Β.P16, U1.IN1
  N6: Station_2Β.3V3, buzzer_module.pin1
  N7: Station_2Β.GND, Station_2Β.Bat_-, buzzer_module.pin3, VCC2.-
  N8: Station_2Β.Bat_+, VCC2.+
  VSS: LCD1.VSS, LCM1602_IIC1.VSS
  VDD: LCD1.VDD, LCM1602_IIC1.VDD
  N9: LCD1.V0, LCM1602_IIC1.V0
  N10: LCD1.RS, LCM1602_IIC1.RS
  N11: LCD1.R/W, LCM1602_IIC1.RW
  N12: LCD1.E, LCM1602_IIC1.E
  N13: LCD1.DB0, LCM1602_IIC1.D0
  N14: LCD1.DB1, LCM1602_IIC1.D1
  N15: LCD1.DB2, LCM1602_IIC1.D2
  N16: LCD1.DB3, LCM1602_IIC1.D3
  N17: LCD1.DB4, LCM1602_IIC1.D4
  N18: LCD1.DB5, LCM1602_IIC1.D5
  N19: LCD1.DB6, LCM1602_IIC1.D6
  N20: LCD1.DB7, LCM1602_IIC1.D7
  N21: LCD1.LED+, LCM1602_IIC1.A
  N22: LCD1.LED-, LCM1602_IIC1.K
  N23: LCM1602_IIC1.GND, VCC1.+
  N24: LCM1602_IIC1.VCC, VCC1.-
  N25: Earthquake_Sensor.Bat_-, VCC3.-
  N26: Earthquake_Sensor.Bat_+, VCC3.+
  N27: Station_2Α.Bat_-, VCC4.-
  N28: Station_2Α.Bat_+, VCC4.+

custom parts:
  Microbit: BBC Microbit Fritzing part. May 2019 expanded to include schematic and pcb views as well as breadboard. PCB view assumes an Adafruit PRODUCT ID: 3342 2x40 Right Angle through hole edge connector (although others will probably work as well). The pcb svg is custom (see forum article http://forum.fritzing.org/t/making-edge-connectors-and-both-side-smd-parts/7287 for an explaination if you need to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
  4-Channel 5v Relay Shield: 4 Channel 5v Relay Shield w. 2x SPD-06VDC-SD-C
  LCM1602 IIC: I2C-Module to use a 1602 or 2004 LCD on with the wire.h libory Serial LCD Modul
  Microbit: BBC Microbit Fritzing part. May 2019 expanded to include schematic and pcb views as well as breadboard. PCB view assumes an Adafruit PRODUCT ID: 3342 2x40 Right Angle through hole edge connector (although others will probably work as well). The pcb svg is custom (see forum article http://forum.fritzing.org/t/making-edge-connectors-and-both-side-smd-parts/7287 for an explaination if you need to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
